# Fritzing sketch Sample (saved by Fritzing 0.3.16b)
breadboards: 1

parts:
  LED1 = Red LED - 5mm
  LED1_2 = Red LED - 5mm
  LED2 = yellow LED - 5mm
  LED2_2 = yellow LED - 5mm
  LED3 = green LED - 5mm
  LED3_2 = green LED - 5mm
  LED4 = Blue LED - 5mm
  LED4_2 = Blue LED - 5mm
  R1 = Resistor [resistance=330 package=THT]
  R1_2 = Resistor [resistance=330 package=THT]
  R1_3 = Resistor [resistance=330 package=THT]
  R1_4 = Resistor [resistance=330 package=THT]
  R1_5 = Resistor [resistance=330 package=THT]
  R1_6 = Resistor [resistance=330 package=THT]
  R1_7 = Resistor [resistance=330 package=THT]
  R1_8 = Resistor [resistance=330 package=THT]
  S1 = Pushbutton [package="[THT]"]
  R2 = Resistor [resistance=10k package=THT]
  R3 = Rotary Potentiometer (Large) [package=THT]
  J1 = female pin header, 6 pins [form="♀ (female)"]
  J1_2 = female pin header, 6 pins [form="♀ (female)"]
  J2 = female pin header, 8 pins [form="♀ (female)"]
  J2_2 = female pin header, 8 pins [form="♀ (female)"]

nets:
  N1: LED1.cathode, R1.Pin_1
  N2: LED1.anode, J2.pin1
  N3: LED1_2.cathode, R1_2.Pin_1
  N4: LED1_2.anode, J2.pin2
  N5: LED2.cathode, R1_3.Pin_1
  N6: LED2.anode, J2.pin3
  N7: LED2_2.cathode, R1_4.Pin_1
  N8: LED2_2.anode, J2.pin4
  N9: LED3.cathode, R1_5.Pin_1
  N10: LED3.anode, J2.pin5
  N11: LED3_2.cathode, R1_6.Pin_1
  N12: LED3_2.anode, J2.pin6
  N13: LED4.cathode, R1_7.Pin_1
  N14: LED4.anode, J2.pin7
  N15: LED4_2.cathode, R1_8.Pin_1
  N16: LED4_2.anode, J2.pin8
  5V: R1.Pin_0, R1_2.Pin_0, R1_3.Pin_0, R1_4.Pin_0, R1_5.Pin_0, R1_6.Pin_0, R1_7.Pin_0, R1_8.Pin_0, S1.Pin_1, S1.Pin_2, R3.leg2, J1_2.pin3
  N17: S1.Pin_3, S1.Pin_4, R2.Pin_1, J2_2.pin5
  GND: R2.Pin_0, R3.leg1, J1_2.pin4
  N18: R3.wiper, J1.pin6
